// Logisim project Addition Function.circ as structural Verilog: 1 circuit, main circuit main
module main (
  input  in_1,
  input  in_2,
  input  in_3,
  input  in_4,
  input  in_5,
  input  in_6,
  output out_7,
  output out_8,
  output out_9,
  output out_10
);

  wire and_1_out, and_2_out, and_3_out, and_4_out, and_5_out, and_6_out, and_7_out, and_8_out, and_10_out,
       and_11_out, not_1_out, not_2_out, not_3_out, not_4_out, not_5_out, or_1_out, or_2_out, or_3_out,
       or_4_out, or_6_out;

  and and_1 (and_1_out, in_1, in_4);
  and and_2 (and_2_out, and_1_out, in_5);
  and and_3 (and_3_out, and_1_out, in_2);
  and and_4 (and_4_out, and_1_out, in_2, in_5);
  and and_5 (and_5_out, in_2, in_5);
  or or_1 (or_1_out, and_5_out, and_4_out, and_3_out, and_2_out);
  not not_1 (not_1_out, and_1_out);
  or or_2 (or_2_out, and_2_out, and_3_out, and_5_out);
  and and_6 (and_6_out, or_2_out, and_4_out);
  not not_2 (not_2_out, in_2);
  not not_3 (not_3_out, in_5);
  or or_3 (or_3_out, in_1, in_4);
  and and_7 (and_7_out, in_5, not_2_out);
  or or_4 (or_4_out, and_7_out, and_8_out);
  and and_8 (and_8_out, not_3_out, in_2);
  and and_9 (out_7, not_1_out, or_3_out);
  and and_10 (and_10_out, and_1_out, not_4_out);
  not not_4 (not_4_out, or_4_out);
  not not_5 (not_5_out, and_1_out);
  and and_11 (and_11_out, not_5_out, or_4_out);
  or or_5 (out_8, and_6_out, or_6_out);
  or or_6 (or_6_out, and_10_out, and_11_out);
endmodule
